# Fritzing sketch binary_clock (saved by Fritzing 0.9.3b)
perfboards: 3

parts:
  U1 = attiny85 [package=dip]
  U2 = 74HC595 [package="DIP16 [THT]"]
  U3 = 74HC595 [package="DIP16 [THT]"]
  LED12 = smd LED [color="Red (633nm)" package="0805 [SMD]"]
  LED16 = smd LED [color="Red (633nm)" package="0805 [SMD]"]
  LED17 = smd LED [color="Red (633nm)" package="0805 [SMD]"]
  LED18 = smd LED [color="Red (633nm)" package="0805 [SMD]"]
  LED19 = smd LED [color="Red (633nm)" package="0805 [SMD]"]
  LED20 = smd LED [color="Red (633nm)" package="0805 [SMD]"]
  LED21 = smd LED [color="Red (633nm)" package="0805 [SMD]"]
  LED22 = smd LED [color="Red (633nm)" package="0805 [SMD]"]
  LED23 = smd LED [color="Red (633nm)" package="0805 [SMD]"]
  LED24 = smd LED [color="Red (633nm)" package="0805 [SMD]"]
  LED25 = smd LED [color="Red (633nm)" package="0805 [SMD]"]
  LED26 = smd LED [color="Red (633nm)" package="0805 [SMD]"]
  LED27 = smd LED [color="Red (633nm)" package="0805 [SMD]"]
  LED28 = smd LED [color="Red (633nm)" package="0805 [SMD]"]
  LED29 = smd LED [color="Red (633nm)" package="0805 [SMD]"]
  LED30 = smd LED [color="Red (633nm)" package="0805 [SMD]"]
  LED31 = LED - 3mm [color="Green (555nm)" current=6mA package="3 mm [THT]"]
  LED32 = LED - 3mm [color="Green (555nm)" current=6mA package="3 mm [THT]"]
  LED33 = LED - 3mm [color="Green (555nm)" current=6mA package="3 mm [THT]"]
  LED34 = LED - 3mm [color="Green (555nm)" current=6mA package="3 mm [THT]"]
  LED35 = LED - 3mm [color="Green (555nm)" current=6mA package="3 mm [THT]"]
  LED36 = LED - 3mm [color="Green (555nm)" current=6mA package="3 mm [THT]"]
  LED37 = LED - 3mm [color="Green (555nm)" current=6mA package="3 mm [THT]"]
  LED38 = LED - 3mm [color="Green (555nm)" current=6mA package="3 mm [THT]"]
  LED39 = LED - 3mm [color="Green (555nm)" current=6mA package="3 mm [THT]"]
  LED40 = LED - 3mm [color="Green (555nm)" current=6mA package="3 mm [THT]"]
  LED41 = LED - 3mm [color="Green (555nm)" current=6mA package="3 mm [THT]"]
  LED42 = LED - 3mm [color="Green (555nm)" current=6mA package="3 mm [THT]"]
  LED43 = LED - 3mm [color="Green (555nm)" current=6mA package="3 mm [THT]"]
  LED44 = LED - 3mm [color="Green (555nm)" current=6mA package="3 mm [THT]"]
  LED45 = LED - 3mm [color="Green (555nm)" current=6mA package="3 mm [THT]"]
  LED46 = LED - 3mm [color="Green (555nm)" current=6mA package="3 mm [THT]"]
  U4 = attiny85 [package=dip]
  U5 = 74HC595 [package="DIP16 [THT]"]
  R1 = Resistor [tolerance=±5% resistance=330 package=THT]
  R2 = Resistor [tolerance=±5% resistance=330 package=THT]
  R3 = Resistor [tolerance=±5% resistance=330 package=THT]
  R4 = Resistor [tolerance=±5% resistance=330 package=THT]
  U6 = attiny85 [package=dip]
  U7 = 74HC595 [package="DIP16 [THT]"]
  LED47 = LED - 3mm [color="Green (555nm)" current=6mA package="3 mm [THT]"]
  LED48 = LED - 3mm [color="Green (555nm)" current=6mA package="3 mm [THT]"]
  LED49 = LED - 3mm [color="Green (555nm)" current=6mA package="3 mm [THT]"]
  LED50 = LED - 3mm [color="Green (555nm)" current=6mA package="3 mm [THT]"]
  LED51 = LED - 3mm [color="Green (555nm)" current=6mA package="3 mm [THT]"]
  LED52 = LED - 3mm [color="Green (555nm)" current=6mA package="3 mm [THT]"]
  LED53 = LED - 3mm [color="Green (555nm)" current=6mA package="3 mm [THT]"]
  LED54 = LED - 3mm [color="Green (555nm)" current=6mA package="3 mm [THT]"]
  LED55 = LED - 3mm [color="Green (555nm)" current=6mA package="3 mm [THT]"]
  LED56 = LED - 3mm [color="Green (555nm)" current=6mA package="3 mm [THT]"]
  LED57 = LED - 3mm [color="Green (555nm)" current=6mA package="3 mm [THT]"]
  LED58 = LED - 3mm [color="Green (555nm)" current=6mA package="3 mm [THT]"]
  LED59 = LED - 3mm [color="Green (555nm)" current=6mA package="3 mm [THT]"]
  LED60 = LED - 3mm [color="Green (555nm)" current=6mA package="3 mm [THT]"]
  LED61 = LED - 3mm [color="Green (555nm)" current=6mA package="3 mm [THT]"]
  LED62 = LED - 3mm [color="Green (555nm)" current=6mA package="3 mm [THT]"]
  R5 = Resistor [tolerance=±5% resistance=330 package=THT]
  R6 = Resistor [tolerance=±5% resistance=330 package=THT]
  R7 = Resistor [tolerance=±5% resistance=330 package=THT]
  R8 = Resistor [tolerance=±5% resistance=330 package=THT]
  S1 = Toggle Switch [package=THT]

nets:
  N1: U1.Pin_3, U3.ST_CP
  N2: U1.Pin_7, U2.DS
  N3: U2.GND, U3.OE
  N4: U2.Q7', U3.DS
  N5: U2.SH_CP, U3.SH_CP
  VCC: U2.VCC, U3.MR, U3.VCC
  N6: LED12.cathode, LED18.anode, LED20.cathode, LED22.anode, LED24.cathode, LED26.anode, LED29.cathode, LED30.anode
  N7: LED16.cathode, LED19.cathode, LED23.cathode, LED28.cathode
  N8: LED17.cathode, LED21.cathode, LED25.cathode, LED27.cathode
  N9: LED31.cathode, LED32.cathode, LED33.cathode, LED34.cathode, U5.Q4
  N10: LED31.anode, LED35.anode, LED39.anode, LED43.anode, R2.Pin_0
  N11: LED32.anode, LED36.anode, LED40.anode, LED44.anode, R3.Pin_0
  N12: LED33.anode, LED37.anode, LED41.anode, LED45.anode, R4.Pin_0
  N13: LED34.anode, LED38.anode, LED42.anode, LED46.anode, R1.Pin_0
  N14: LED35.cathode, LED36.cathode, LED37.cathode, LED38.cathode, U5.Q5
  N15: LED39.cathode, LED40.cathode, LED41.cathode, LED42.cathode, U5.Q6
  N16: LED43.cathode, LED44.cathode, LED45.cathode, LED46.cathode, U5.Q7
  N17: U4.Pin_2, U5.SH_CP
  N18: U4.Pin_3, U5.ST_CP
  N19: U4.Pin_4, U5.GND, U5.OE
  N20: U4.Pin_7, U5.DS
  N21: U4.Pin_8, U5.MR, U5.VCC
  N22: U5.Q1, R4.Pin_1
  N23: U5.Q2, R3.Pin_1
  N24: U5.Q3, R2.Pin_1
  N25: U5.Q0, R1.Pin_1
  N26: U6.Pin_2, U7.SH_CP
  N27: U6.Pin_3, U7.ST_CP
  N28: U6.Pin_4, U7.GND, S1.L1
  N29: U6.Pin_7, U7.DS
  N30: U6.Pin_8, U7.MR, U7.VCC, S1.L2
  N31: U7.Q1, LED48.anode, LED49.anode, LED50.anode, LED54.anode
  N32: U7.Q2, LED58.anode, LED59.anode, LED60.anode, LED61.anode
  N33: U7.Q3, LED47.anode, LED55.anode, LED56.anode, LED57.anode
  N34: U7.Q4, R8.Pin_1
  N35: U7.Q5, R5.Pin_1
  N36: U7.Q6, R6.Pin_1
  N37: U7.Q7, R7.Pin_1
  N38: U7.OE, S1.COM
  N39: U7.Q0, LED51.anode, LED52.anode, LED53.anode, LED62.anode
  N40: LED47.cathode, LED51.cathode, LED54.cathode, LED58.cathode, R7.Pin_0
  N41: LED48.cathode, LED55.cathode, LED59.cathode, LED62.cathode, R5.Pin_0
  N42: LED49.cathode, LED52.cathode, LED56.cathode, LED60.cathode, R8.Pin_0
  N43: LED50.cathode, LED53.cathode, LED57.cathode, LED61.cathode, R6.Pin_0
